# Fritzing sketch FritzingSchem (saved by Fritzing 0.9.3b)
breadboards: 1

parts:
  ARDUINO1 = Arduino Micro
  Bauteil1 = Adafruit TCA9548A
  Bauteil2 = Adafruit ADS1015 12Bit I2C ADC [part_number="Adafruit #1083"]
  IC1 = IC, DIP package, 8 pins [chip_label=LM358]
  C1 = Tantalum Capacitor [capacitance=1μF package="100 mil [THT, tantalum]"]
  Photodiode = LED - 5mm [color="Red (633nm)" package="5 mm [THT]"]
  R1 = Resistor [tolerance=±5% resistance=220 package=THT]

nets:
  N1: ARDUINO1.D2, Bauteil1.INPUTSDA
  N2: ARDUINO1.D3, Bauteil1.INPUTSCL, Bauteil2.SCL
  N3: Bauteil1.0SDA, Bauteil2.SDA
  N4: Bauteil2.AIN0, IC1.pin7, C1.-, Photodiode.cathode, R1.Pin_0
  N5: IC1.pin6, C1.+, R1.Pin_1

custom parts:
  Arduino Micro: Arduino Micro Microcontroller
  Adafruit TCA9548A: You just found the perfect I2C sensor, and you want to wire up two or three or more of them to your Arduino when you realize "Uh oh, this chip has a fixed I2C address, and from what I know about I2C, you cannot have two devices with the same address on the same SDA/SCL pins!" Are you out of luck? You would be, if you didn't have this ultra-cool TCA9548A 1-to-8 I2C multiplexer! Finally, a way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
  Adafruit ADS1015 12Bit I2C ADC: For microcontrollers without an analog-to-digital converter or when you want a higher-precision ADC, the ADS1015 provides 12-bit precision at 3300 samples/second over I2C. The chip can be configured as 4 single-ended input channels, or two differential channels. As a nice bonus, it even includes a programmable gain amplifier, up to x16, to help boost up smaller single/differential signals to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
