# Fritzing sketch TransimpSchem (saved by Fritzing 0.9.3b)
breadboards: 1

parts:
  LM358 = IC, DIP package, 8 pins [chip_label=LM358]
  PD = LED - 5mm [color="Infrared (940nm)" package="5 mm [THT]"]
  C1 = Tantalum Capacitor [capacitance=1pF package="100 mil [THT, tantalum]"]
  R2 = Resistor [tolerance=±5% resistance=1M package=THT]
  C2 = Tantalum Capacitor [capacitance=1pF package="100 mil [THT, tantalum]"]
  R1 = Resistor [tolerance=±5% resistance=1M package=THT]
  PD1 = LED - 5mm [color="Infrared (940nm)" package="5 mm [THT]"]

nets:
  Out1: LM358.pin1, LM358.pin2, R2.Pin_0, PD1.cathode
  GND: LM358.pin3, LM358.pin4, LM358.pin5, PD.anode, PD1.anode
  N1: LM358.pin6, R1.Pin_0
  Out2: LM358.pin7, PD.cathode
  5V: LM358.pin8
  N2: C1.-, R1.Pin_1
  N3: R2.Pin_1, C2.-
